// Logisim project cpu.circ as structural Verilog: 1 circuit, main circuit main
module main (
);

  wire and_1_out, clock_1_out, HLT, JMP, not_1_out, PCE, PCO;
  wire [4:0] pull_resistor_5_node;
  wire [10:0] controlled_buffer_1_out, controlled_buffer_2_out, ProgramCounter_q;

  Clock clock_1 (.out(clock_1_out));
  Counter #(.max('h7ff), .width(11)) ProgramCounter (
    .count(PCE), .clk(and_1_out), .D(controlled_buffer_1_out), .Q(ProgramCounter_q));  // open: clr, load, up, carry
  assign controlled_buffer_1_out = JMP ? controlled_buffer_2_out : 11'bz;  // Controlled_Buffer controlled_buffer_1
  not not_1 (not_1_out, HLT);
  and and_1 (and_1_out, clock_1_out, not_1_out);
  LED led_1 (.in(pull_resistor_5_node[4]));
  LED led_2 (.in(pull_resistor_5_node[3]));
  LED led_3 (.in(pull_resistor_5_node[2]));
  assign controlled_buffer_2_out = PCO ? ProgramCounter_q : 11'bz;  // Controlled_Buffer controlled_buffer_2
  Pull_Resistor pull_resistor_1 (.node(pull_resistor_5_node[4]));
  LED led_4 (.in(pull_resistor_5_node[1]));
  LED led_5 (.in(pull_resistor_5_node[0]));
  LED led_6 (.in(controlled_buffer_2_out[10]));
  LED led_7 (.in(controlled_buffer_2_out[9]));
  Pull_Resistor pull_resistor_2 (.node(pull_resistor_5_node[3]));
  Pull_Resistor pull_resistor_3 (.node(pull_resistor_5_node[2]));
  Pull_Resistor pull_resistor_4 (.node(pull_resistor_5_node[1]));
  Pull_Resistor pull_resistor_5 (.node(pull_resistor_5_node[0]));
  LED led_8 (.in(controlled_buffer_2_out[8]));
  LED led_9 (.in(controlled_buffer_2_out[7]));
  LED led_10 (.in(controlled_buffer_2_out[6]));
  LED led_11 (.in(controlled_buffer_2_out[5]));
  Pull_Resistor pull_resistor_6 (.node(controlled_buffer_2_out[10]));
  Pull_Resistor pull_resistor_7 (.node(controlled_buffer_2_out[9]));
  Pull_Resistor pull_resistor_8 (.node(controlled_buffer_2_out[8]));
  Pull_Resistor pull_resistor_9 (.node(controlled_buffer_2_out[7]));
  Pull_Resistor pull_resistor_10 (.node(controlled_buffer_2_out[6]));
  Pull_Resistor pull_resistor_11 (.node(controlled_buffer_2_out[5]));
  LED led_12 (.in(controlled_buffer_2_out[4]));
  LED led_13 (.in(controlled_buffer_2_out[3]));
  LED led_14 (.in(controlled_buffer_2_out[2]));
  LED led_15 (.in(controlled_buffer_2_out[1]));
  Pull_Resistor pull_resistor_12 (.node(controlled_buffer_2_out[4]));
  Pull_Resistor pull_resistor_13 (.node(controlled_buffer_2_out[3]));
  Pull_Resistor pull_resistor_14 (.node(controlled_buffer_2_out[2]));
  Pull_Resistor pull_resistor_15 (.node(controlled_buffer_2_out[1]));
  Pull_Resistor pull_resistor_16 (.node(controlled_buffer_2_out[0]));
  LED led_16 (.in(controlled_buffer_2_out[0]));
endmodule
